// Logisim project 8051.circ as structural Verilog: 3 circuits, main circuit main
module main (
  input  [7:0] in_1,
  input  [3:0] in_2,
  input  Reset
);

  wire clock_1_out, d_ff_1_q, d_ff_2_q, d_ff_3_q, undriven, undriven_2, undriven_3;
  wire [7:0] ALU_buffer1_q, ALU_buffer2_q, alu_v2_1_accumulator, register_1_q;

  Register ALU_buffer1 (.D(register_1_q), .en(1'b1), .clk(clock_1_out), .Q(ALU_buffer1_q), .clr(Reset));
  Register ALU_buffer2 (.D(in_1), .en(1'b1), .clk(clock_1_out), .Q(ALU_buffer2_q), .clr(Reset));
  Clock clock_1 (.out(clock_1_out));
  D_Flip_Flop d_ff_1 (.D(undriven_2), .clk(clock_1_out), .Q(d_ff_1_q), .reset(Reset));  // open: Qn, preset
  D_Flip_Flop d_ff_2 (.D(undriven_3), .clk(clock_1_out), .Q(d_ff_2_q), .reset(Reset));  // open: Qn, preset
  D_Flip_Flop d_ff_3 (.D(undriven), .clk(clock_1_out), .Q(d_ff_3_q), .reset(Reset));  // open: Qn, preset
  Register register_1 (.D(alu_v2_1_accumulator), .en(1'b1), .clk(clock_1_out), .Q(register_1_q), .clr(Reset));
  ALU_v2 alu_v2_1 (
    .OverflowIn(undriven), .AuxiliaryCarryIn(undriven_3), .CarryIn(undriven_2), .Buffer1(ALU_buffer1_q),
    .Buffer2(ALU_buffer2_q), .Opcode(in_2), .Accumulator(alu_v2_1_accumulator), .CarryFlag(d_ff_1_q),
    .AuxiliaryCarryFlag(d_ff_2_q), .OverflowFlag(d_ff_3_q));  // open: ZeroFlag, SignFlag
endmodule

module ALU_v2 (
  input  OverflowIn,
  input  AuxiliaryCarryIn,
  input  CarryIn,
  input  [7:0] Buffer1,
  input  [7:0] Buffer2,
  input  [3:0] Opcode,
  output [7:0] Accumulator,
  output CarryFlag,
  output ZeroFlag,
  output SignFlag,
  output AuxiliaryCarryFlag,
  output OverflowFlag
);

  wire adder_4_cout, adder_5_cout, adder_6_cout, adder_7_cout, adder_8_cout, adder_10_cout, comparator_1_lt,
       comparator_2_lt, comparator_3_lt, nor_1_out, or_1_out, xor_1_out, xor_2_out, xor_4_out;
  wire [6:0] adder_9_out, negator_2_out;
  wire [7:0] adder_1_out, adder_2_out, adder_3_out, adder_4_out, adder_5_out, adder_6_out, and_1_out,
       divider_1_out, divider_1_rem, multiplier_1_out, negator_1_out, or_2_out, undriven, xor_3_out;
  wire [15:0] bit_extender_1_out, bit_extender_2_out;
  wire [15:8] multiplier_1_out_2;

  Adder adder_1 (.a({8{1'b0}}), .b(Buffer2), .out(adder_1_out), .cin(CarryIn));  // open: cout
  Negator negator_1 (.in(adder_1_out), .out(negator_1_out));
  assign bit_extender_1_out = {{8{Buffer2[7]}}, Buffer2};  // Bit_Extender bit_extender_1
  assign bit_extender_2_out = {{8{Buffer1[7]}}, Buffer1};  // Bit_Extender bit_extender_2
  Comparator #(.mode("unsigned")) comparator_1 (.a(Buffer1), .b(Buffer2), .lt(comparator_1_lt));  // open: gt, eq
  Adder adder_2 (.a(8'h1), .b(Buffer1), .out(adder_2_out));  // open: cin, cout
  Adder adder_3 (.a({8{1'b1}}), .b(Buffer1), .out(adder_3_out));  // open: cin, cout
  Adder adder_4 (.a(Buffer1), .b(Buffer2), .out(adder_4_out), .cout(adder_4_cout));  // open: cin
  Adder adder_5 (.a(Buffer1), .b(Buffer2), .out(adder_5_out), .cin(CarryIn), .cout(adder_5_cout));
  Adder adder_6 (.a(Buffer1), .b(negator_1_out), .out(adder_6_out), .cout(adder_6_cout));  // open: cin
  Multiplier #(.width(16)) multiplier_1 (
    .a(bit_extender_1_out), .b(bit_extender_2_out), .out({multiplier_1_out_2, multiplier_1_out}));  // open: cin, cout
  Adder #(.width(4)) adder_7 (.a(Buffer1[3:0]), .b(Buffer2[3:0]), .cout(adder_7_cout));  // open: out, cin
  Adder #(.width(4)) adder_8 (.a(Buffer1[3:0]), .b(Buffer2[3:0]), .cin(CarryIn), .cout(adder_8_cout));  // open: out
  xor xor_1 (xor_1_out, CarryIn, adder_4_cout);
  Divider divider_1 (.a(Buffer1), .b(Buffer2), .out(divider_1_out), .rem(divider_1_rem));  // open: upper
  Comparator #(.mode("unsigned"), .width(4)) comparator_2 (
    .a(Buffer1[3:0]), .b(Buffer2[3:0]), .lt(comparator_2_lt));  // open: gt, eq
  xor xor_2 (xor_2_out, CarryIn, adder_5_cout);
  or or_1 (or_1_out, multiplier_1_out_2[8], multiplier_1_out_2[9], multiplier_1_out_2[10], multiplier_1_out_2[11], multiplier_1_out_2[12], multiplier_1_out_2[13], multiplier_1_out_2[14], multiplier_1_out_2[15]);
  nor nor_1 (nor_1_out, Buffer2[0], Buffer2[1], Buffer2[2], Buffer2[3], Buffer2[4], Buffer2[5], Buffer2[6], Buffer2[7]);
  // NoConnect on undriven
  assign or_2_out = Buffer1 | Buffer2;  // OR_Gate or_2, 8 bits wide
  assign and_1_out = Buffer1 & Buffer2;  // AND_Gate and_1, 8 bits wide
  assign xor_3_out = Buffer1 ^ Buffer2;  // XOR_Gate xor_3, 8 bits wide
  Comparator comparator_3 (.a(Buffer1), .b(Buffer2), .lt(comparator_3_lt));  // open: gt, eq
  Comparator #(.mode("unsigned")) comparator_4 (.a(Buffer1), .b(Buffer2), .eq(ZeroFlag), .lt(SignFlag));  // open: gt
  Adder #(.width(7)) adder_9 (.a({7{1'b0}}), .b(Buffer2[6:0]), .out(adder_9_out), .cin(CarryIn));  // open: cout
  Multiplexer #(.select(4), .width(8)) multiplexer_1 (
    .in0(adder_2_out), .in1(adder_3_out), .in2(adder_4_out), .in3(adder_5_out), .in4(adder_6_out),
    .in5(multiplier_1_out), .in6(divider_1_out), .in7(or_2_out), .in8(and_1_out), .in9(xor_3_out),
    .in10(undriven), .in15(Buffer1), .out(Accumulator), .sel(Opcode));  // open: in11, in12, in13, in14
  // Probe on multiplier_1_out_2
  // Probe on divider_1_rem
  Adder #(.width(7)) adder_10 (.a(Buffer1[6:0]), .b(negator_2_out), .cout(adder_10_cout));  // open: out, cin
  Negator #(.width(7)) negator_2 (.in(adder_9_out), .out(negator_2_out));
  xor xor_4 (xor_4_out, adder_6_cout, adder_10_cout);
  Multiplexer #(.select(4)) multiplexer_2 (
    .in0(CarryIn), .in1(CarryIn), .in2(adder_4_cout), .in3(adder_5_cout), .in4(comparator_1_lt), .in5(1'b0),
    .in6(1'b0), .in7(CarryIn), .in8(CarryIn), .in9(CarryIn), .in10(comparator_3_lt), .out(CarryFlag),
    .sel(Opcode));  // open: in11, in12, in13, in14, in15
  Multiplexer #(.select(4)) multiplexer_3 (
    .in0(CarryIn), .in1(CarryIn), .in2(adder_7_cout), .in3(adder_8_cout), .in4(comparator_2_lt),
    .in5(AuxiliaryCarryIn), .in6(AuxiliaryCarryIn), .in7(AuxiliaryCarryIn), .in8(AuxiliaryCarryIn),
    .in9(AuxiliaryCarryIn), .in10(AuxiliaryCarryIn), .out(AuxiliaryCarryFlag), .sel(Opcode));  // open: in11, in12, in13, in14, in15
  Multiplexer #(.select(4)) multiplexer_4 (
    .in0(CarryIn), .in1(CarryIn), .in2(xor_1_out), .in3(xor_2_out), .in4(xor_4_out), .in5(or_1_out),
    .in6(nor_1_out), .in7(OverflowIn), .in8(OverflowIn), .in9(OverflowIn), .in10(OverflowIn),
    .out(OverflowFlag), .sel(Opcode));  // open: in11, in12, in13, in14, in15

  // Notes on the sheet:
  //   ALU ->
  //   ->
  //   cin
  //   A
  //   B
  //   to register B
endmodule

module InstructionDecoder (
  input  [7:0] InstructionLine,
  input  Clock,
  output [7:0] EffectiveAddress,
  output [7:0] Data,
  output RegisterLoad,
  output RegisterStore,
  output RegisterTransfer,
  output IncrementPC,
  output MemoryRead,
  output MemoryWrite,
  output MemoryEnable
);

  Register register_1 (.clk(Clock), .Q(Data));  // open: D, en, clr

  // Notes on the sheet:
  //   Operand
  //   Operation code
endmodule
